// Logisim project DistribuidorPortaMultiBitEXOR.circ as structural Verilog: 1 circuit, main circuit main
module main (
);

  wire [3:0] xor_1_out;

  Hex_Digit_Display hex_digit_display_1 (.value(4'b1010));  // open: dp
  xor xor_1 (xor_1_out[0], 1'b0, 1'b0);
  xor xor_2 (xor_1_out[1], 1'b0, 1'b1);
  xor xor_3 (xor_1_out[2], 1'b0, 1'b0);
  xor xor_4 (xor_1_out[3], 1'b0, 1'b1);
  Hex_Digit_Display hex_digit_display_2 (.value(xor_1_out));  // open: dp

  // Notes on the sheet:
  //   Entrada de 4 bits
  //   Distribuidor separa barramento de 4 bits em 4 linhas de 1 bit
  //   A porta XOR é uma porta lógica digital que fornece uma saída verdadeira quando o número de entradas verdadeiras é ímpar.
  //   barramento de 4 bits
  //   Se esta entrada = 0 então faz uma cópia (0101 continua 0101)
  //   Se esta entrada = 1 então complementa (0101 vira 1010)
  //   Entrada de 1 bit
  //   Estas quatro portas XOR equivalem àquela porta de 4 bits
  //   linha de um bit
  //   Distribuidor junta 4 linhas de 1 bit em barramento de 4 bits
endmodule
