// Logisim project decodificador.circ as structural Verilog: 1 circuit, main circuit decodificador
module decodificador (
  input  [3:0] in_1,
  output [3:0] out_2
);

  wire nand_1_out, nand_2_out, nand_3_out, nand_4_out, nand_5_out, nand_6_out, nand_7_out, nand_8_out,
       nand_9_out, nand_10_out, nand_11_out, nand_12_out, nand_13_out, nand_14_out, nand_15_out, nand_16_out,
       nand_17_out, nand_18_out, nand_19_out, nand_20_out, nand_21_out, nand_22_out, nand_23_out,
       nand_24_out, nand_25_out, nand_26_out, nand_27_out, nand_29_out, nand_30_out;
  wire [2:1] undriven;
  wire [3:0] undriven_2;

  nand nand_1 (nand_1_out, undriven[1], undriven[1]);
  nand nand_2 (nand_2_out, undriven[2], undriven[2]);
  nand nand_3 (nand_3_out, undriven[2], undriven[2]);
  nand nand_4 (nand_4_out, undriven_2[3], undriven_2[3]);
  nand nand_5 (nand_5_out, undriven_2[0], undriven_2[0]);
  nand nand_6 (nand_6_out, undriven[1], undriven[1]);
  nand nand_7 (nand_7_out, undriven[2], nand_1_out);
  nand nand_8 (nand_8_out, undriven_2[3], nand_2_out);
  nand nand_9 (nand_9_out, undriven_2[3], nand_3_out);
  nand nand_10 (nand_10_out, nand_4_out, undriven[1]);
  nand nand_11 (nand_11_out, undriven[1], nand_5_out);
  nand nand_12 (nand_12_out, undriven_2[3], nand_6_out);
  nand nand_13 (nand_13_out, undriven_2[3], undriven_2[3]);
  nand nand_14 (nand_14_out, nand_7_out, nand_7_out);
  nand nand_15 (nand_15_out, undriven_2[0], undriven_2[0]);
  nand nand_16 (nand_16_out, nand_8_out, nand_8_out);
  nand nand_17 (nand_17_out, nand_9_out, nand_9_out);
  nand nand_18 (nand_18_out, nand_10_out, nand_11_out);
  nand nand_19 (nand_19_out, nand_12_out, nand_12_out);
  nand nand_20 (nand_20_out, nand_13_out, undriven[2]);
  nand nand_21 (nand_21_out, nand_14_out, nand_15_out);
  nand nand_22 (nand_22_out, nand_16_out, undriven_2[0]);
  nand nand_23 (nand_23_out, nand_17_out, undriven[1]);
  nand nand_24 (nand_24_out, nand_18_out, nand_18_out);
  nand nand_25 (nand_25_out, nand_19_out, undriven_2[0]);
  nand nand_26 (nand_26_out, nand_20_out, nand_21_out);
  nand nand_27 (nand_27_out, nand_22_out, nand_23_out);
  nand nand_28 (undriven_2[1], nand_24_out, nand_25_out);
  nand nand_29 (nand_29_out, nand_26_out, nand_26_out);
  nand nand_30 (nand_30_out, nand_27_out, nand_27_out);
  nand nand_31 (undriven_2[2], nand_29_out, nand_30_out);
endmodule
