// Logisim project somador-subtrator.circ as structural Verilog: 6 circuits, main circuit main
module main (
  input  in_1
);

  wire somador_4bits_2_2bits_1_cout;
  wire [3:0] somador_4bits_2_2bits_1_somas_parciais, xor_1_out;

  LED led_1 (.in(1'b0));
  LED led_2 (.in(1'b1));
  LED led_3 (.in(1'b0));
  LED led_4 (.in(1'b1));
  LED led_5 (.in(1'b1));
  LED led_6 (.in(1'b1));
  LED led_7 (.in(1'b0));
  LED led_8 (.in(1'b0));
  Hex_Digit_Display hex_digit_display_1 (.value(4'b0111));  // open: dp
  Hex_Digit_Display hex_digit_display_2 (.value(4'b0100));  // open: dp
  assign xor_1_out = {4{in_1}} ^ 4'b0111;  // XOR_Gate xor_1, 4 bits wide
  Hex_Digit_Display hex_digit_display_3 (.value(xor_1_out));  // open: dp
  somador_4bits_2_2bits somador_4bits_2_2bits_1 (
    .Cin(in_1), .Cout(somador_4bits_2_2bits_1_cout), .B(xor_1_out), .A(4'b0100),
    .Somas_Parciais(somador_4bits_2_2bits_1_somas_parciais));
  LED led_9 (.in(somador_4bits_2_2bits_1_cout));
  LED led_10 (.in(somador_4bits_2_2bits_1_somas_parciais[3]));
  LED led_11 (.in(somador_4bits_2_2bits_1_somas_parciais[2]));
  LED led_12 (.in(somador_4bits_2_2bits_1_somas_parciais[1]));
  LED led_13 (.in(somador_4bits_2_2bits_1_somas_parciais[0]));
  Hex_Digit_Display hex_digit_display_4 (.value(somador_4bits_2_2bits_1_somas_parciais));  // open: dp
  LED led_14 (.in(somador_4bits_2_2bits_1_somas_parciais[3]));
  Hex_Digit_Display hex_digit_display_5 (.value({1'b0, somador_4bits_2_2bits_1_somas_parciais[2:0]}));  // open: dp

  // Notes on the sheet:
  //   operando B (em complemento de dois)
  //   operando A (em complemento de dois)
  //   0:soma; 1: subtrai
  //   Porta XOR de 4 bits
  //   resultado
  //   A porta XOR de 4 bits é detalhada no DistribuidorPortaMultiBitEXOR.circ
  //   resultado = A {+,-} B
endmodule

module meio_somador (
  input  A,
  input  B,
  output Soma,
  output Cout
);

  xor xor_1 (Soma, A, B);
  and and_1 (Cout, A, B);
endmodule

module somador_completo_1bit (
  input  A,
  input  B,
  input  Cin,
  output Soma_Total,
  output Cout
);

  wire meio_somador_1_cout, meio_somador_1_soma, meio_somador_2_cout;

  meio_somador meio_somador_1 (.A(A), .B(B), .Soma(meio_somador_1_soma), .Cout(meio_somador_1_cout));
  meio_somador meio_somador_2 (.A(meio_somador_1_soma), .B(Cin), .Soma(Soma_Total), .Cout(meio_somador_2_cout));
  or or_1 (Cout, meio_somador_1_cout, meio_somador_2_cout);
endmodule

module somador_2bits (
  input  [1:0] B,
  input  [1:0] A,
  input  Cin,
  output Cout,
  output [1:0] Somas_Parciais
);

  wire somador_completo_1bit_1_cout;

  somador_completo_1bit somador_completo_1bit_1 (
    .A(A[0]), .B(B[0]), .Cin(Cin), .Soma_Total(Somas_Parciais[0]), .Cout(somador_completo_1bit_1_cout));
  somador_completo_1bit somador_completo_1bit_2 (
    .A(A[1]), .B(B[1]), .Cin(somador_completo_1bit_1_cout), .Soma_Total(Somas_Parciais[1]), .Cout(Cout));

  // Notes on the sheet:
  //   São dois somadores de 1bit
endmodule

module somador_4bits_4_1bit (
  input  [3:0] A,
  input  [3:0] B,
  input  Cin,
  output Cout,
  output [3:0] Somas_Parciais
);

  wire somador_completo_1bit_1_cout, somador_completo_1bit_2_cout, somador_completo_1bit_3_cout;

  somador_completo_1bit somador_completo_1bit_1 (
    .A(A[0]), .B(B[0]), .Cin(Cin), .Soma_Total(Somas_Parciais[0]), .Cout(somador_completo_1bit_1_cout));
  somador_completo_1bit somador_completo_1bit_2 (
    .A(A[1]), .B(B[1]), .Cin(somador_completo_1bit_1_cout), .Soma_Total(Somas_Parciais[1]),
    .Cout(somador_completo_1bit_2_cout));
  somador_completo_1bit somador_completo_1bit_3 (
    .A(A[2]), .B(B[2]), .Cin(somador_completo_1bit_2_cout), .Soma_Total(Somas_Parciais[2]),
    .Cout(somador_completo_1bit_3_cout));
  somador_completo_1bit somador_completo_1bit_4 (
    .A(A[3]), .B(B[3]), .Cin(somador_completo_1bit_3_cout), .Soma_Total(Somas_Parciais[3]), .Cout(Cout));
endmodule

module somador_4bits_2_2bits (
  input  [3:0] B,
  input  [3:0] A,
  input  Cin,
  output Cout,
  output [3:0] Somas_Parciais
);

  wire somador_2bits_1_cout;

  LED led_1 (.in(B[0]));
  LED led_2 (.in(B[1]));
  LED led_3 (.in(B[2]));
  LED led_4 (.in(B[3]));
  somador_2bits somador_2bits_1 (
    .Cin(Cin), .Cout(somador_2bits_1_cout), .B(B[1:0]), .A(A[1:0]), .Somas_Parciais(Somas_Parciais[1:0]));
  LED led_5 (.in(Somas_Parciais[0]));
  LED led_6 (.in(Somas_Parciais[1]));
  LED led_7 (.in(Somas_Parciais[2]));
  LED led_8 (.in(Somas_Parciais[3]));
  LED led_9 (.in(A[0]));
  LED led_10 (.in(A[1]));
  LED led_11 (.in(A[2]));
  LED led_12 (.in(A[3]));
  somador_2bits somador_2bits_2 (
    .Cin(somador_2bits_1_cout), .Cout(Cout), .B(B[3:2]), .A(A[3:2]), .Somas_Parciais(Somas_Parciais[3:2]));

  // Notes on the sheet:
  //   A contagem da ordem dos elementos começa pelo que está mais à direita
endmodule
