// Logisim project resolução-ep1.circ as structural Verilog: 7 circuits, main circuit main
module main (
);

  wire somador_4bits_2_2bits_1_cout;
  wire [2:0] decodificador3_3_out_2;
  wire [3:0] decodificador3_1_out_2, decodificador3_2_out_2, somador_4bits_2_2bits_1_somas_parciais,
       xor_1_out;
  wire [3:3] decodificador3_3_out_2_2;

  LED led_1 (.in(1'b0));
  Hex_Digit_Display hex_digit_display_1 (.value(4'b0001));  // open: dp
  LED led_2 (.in(1'b0));
  LED led_3 (.in(1'b0));
  LED led_4 (.in(1'b0));
  LED led_5 (.in(1'b1));
  LED led_6 (.in(1'b1));
  LED led_7 (.in(1'b0));
  LED led_8 (.in(1'b1));
  LED led_9 (.in(1'b0));
  LED led_10 (.in(1'b1));
  Hex_Digit_Display hex_digit_display_2 (.value(4'b0010));  // open: dp
  Hex_Digit_Display hex_digit_display_3 (.value(4'b0001));  // open: dp
  Hex_Digit_Display hex_digit_display_4 (.value(4'b1010));  // open: dp
  LED led_11 (.in(decodificador3_1_out_2[3]));
  decodificador3 decodificador3_1 (.in_1(4'b0001), .out_2(decodificador3_1_out_2));
  decodificador3 decodificador3_2 (.in_1(4'b1010), .out_2(decodificador3_2_out_2));
  LED led_12 (.in(decodificador3_1_out_2[1]));
  LED led_13 (.in(decodificador3_1_out_2[2]));
  LED led_14 (.in(decodificador3_2_out_2[3]));
  LED led_15 (.in(decodificador3_2_out_2[1]));
  LED led_16 (.in(decodificador3_2_out_2[2]));
  LED led_17 (.in(decodificador3_1_out_2[0]));
  Hex_Digit_Display hex_digit_display_5 (.value(decodificador3_1_out_2));  // open: dp
  LED led_18 (.in(decodificador3_2_out_2[0]));
  Hex_Digit_Display hex_digit_display_6 (.value(decodificador3_2_out_2));  // open: dp
  assign xor_1_out = 4'b1111 ^ decodificador3_1_out_2;  // XOR_Gate xor_1, 4 bits wide
  Hex_Digit_Display hex_digit_display_7 (.value(xor_1_out));  // open: dp
  somador_4bits_2_2bits somador_4bits_2_2bits_1 (
    .Cin(1'b1), .Cout(somador_4bits_2_2bits_1_cout), .B(xor_1_out), .A(decodificador3_2_out_2),
    .Somas_Parciais(somador_4bits_2_2bits_1_somas_parciais));
  LED led_19 (.in(somador_4bits_2_2bits_1_somas_parciais[3]));
  Hex_Digit_Display hex_digit_display_8 (.value(somador_4bits_2_2bits_1_somas_parciais));  // open: dp
  LED led_20 (.in(somador_4bits_2_2bits_1_cout));
  LED led_21 (.in(somador_4bits_2_2bits_1_somas_parciais[2]));
  LED led_22 (.in(somador_4bits_2_2bits_1_somas_parciais[1]));
  LED led_23 (.in(somador_4bits_2_2bits_1_somas_parciais[0]));
  LED led_24 (.in(decodificador3_3_out_2_2[3]));
  Hex_Digit_Display hex_digit_display_9 (.value({decodificador3_3_out_2_2[3], decodificador3_3_out_2}));  // open: dp
  decodificador3 decodificador3_3 (
    .in_1(somador_4bits_2_2bits_1_somas_parciais),
    .out_2({decodificador3_3_out_2_2[3], decodificador3_3_out_2}));
  Hex_Digit_Display hex_digit_display_10 (.value({1'b0, decodificador3_3_out_2}));  // open: dp

  // Notes on the sheet:
  //   Entrada B
  //   Entrada A
  //   notação sinal-magnitude
  //   notação sinal-magnitude
  //   sinal-magnitude para complemento de dois
  //   notação complemento de dois
  //   notação complemento de dois
  //   0:soma; 1: subtrai
  //   A +/- B
  //   complemento de dois
  //   para
  //   sinal-magnitude
  //   resultado = A {+,-} B
endmodule

module decodificador3 (
  input  [3:0] in_1,
  output [3:0] out_2
);

  wire nand_1_out, nand_2_out, nand_3_out, nand_4_out, nand_5_out, nand_6_out, nand_7_out, nand_8_out,
       nand_9_out, nand_10_out, nand_11_out, nand_12_out, nand_13_out, nand_14_out, nand_15_out, nand_16_out,
       nand_17_out, nand_18_out, nand_19_out, nand_20_out, nand_21_out, nand_22_out, nand_23_out,
       nand_24_out, nand_25_out, nand_26_out, nand_27_out, nand_29_out, nand_30_out;

  Hex_Digit_Display hex_digit_display_1 (.value(in_1));  // open: dp
  nand nand_1 (nand_1_out, in_1[1], in_1[1]);
  nand nand_2 (nand_2_out, in_1[2], in_1[2]);
  nand nand_3 (nand_3_out, in_1[2], in_1[2]);
  nand nand_4 (nand_4_out, in_1[3], in_1[3]);
  nand nand_5 (nand_5_out, in_1[0], in_1[0]);
  nand nand_6 (nand_6_out, in_1[1], in_1[1]);
  nand nand_7 (nand_7_out, in_1[2], nand_1_out);
  nand nand_8 (nand_8_out, in_1[3], nand_2_out);
  nand nand_9 (nand_9_out, in_1[3], nand_3_out);
  nand nand_10 (nand_10_out, nand_4_out, in_1[1]);
  nand nand_11 (nand_11_out, in_1[1], nand_5_out);
  nand nand_12 (nand_12_out, in_1[3], nand_6_out);
  nand nand_13 (nand_13_out, in_1[3], in_1[3]);
  nand nand_14 (nand_14_out, nand_7_out, nand_7_out);
  nand nand_15 (nand_15_out, in_1[0], in_1[0]);
  nand nand_16 (nand_16_out, nand_8_out, nand_8_out);
  nand nand_17 (nand_17_out, nand_9_out, nand_9_out);
  nand nand_18 (nand_18_out, nand_10_out, nand_11_out);
  nand nand_19 (nand_19_out, nand_12_out, nand_12_out);
  nand nand_20 (nand_20_out, nand_13_out, in_1[2]);
  nand nand_21 (nand_21_out, nand_14_out, nand_15_out);
  nand nand_22 (nand_22_out, nand_16_out, in_1[0]);
  nand nand_23 (nand_23_out, nand_17_out, in_1[1]);
  nand nand_24 (nand_24_out, nand_18_out, nand_18_out);
  nand nand_25 (nand_25_out, nand_19_out, in_1[0]);
  nand nand_26 (nand_26_out, nand_20_out, nand_21_out);
  nand nand_27 (nand_27_out, nand_22_out, nand_23_out);
  nand nand_28 (out_2[1], nand_24_out, nand_25_out);
  nand nand_29 (nand_29_out, nand_26_out, nand_26_out);
  nand nand_30 (nand_30_out, nand_27_out, nand_27_out);
  nand nand_31 (out_2[2], nand_29_out, nand_30_out);
  Hex_Digit_Display hex_digit_display_2 (.value({in_1[3], out_2[2:1], in_1[0]}));  // open: dp

  assign {out_2[3], out_2[0]} = {in_1[3], in_1[0]};
endmodule

module meio_somador (
  input  A,
  input  B,
  output Soma,
  output Cout
);

  xor xor_1 (Soma, A, B);
  and and_1 (Cout, A, B);
endmodule

module somador_completo_1bit (
  input  A,
  input  B,
  input  Cin,
  output Soma_Total,
  output Cout
);

  wire meio_somador_1_cout, meio_somador_1_soma, meio_somador_2_cout;

  meio_somador meio_somador_1 (.A(A), .B(B), .Soma(meio_somador_1_soma), .Cout(meio_somador_1_cout));
  meio_somador meio_somador_2 (.A(meio_somador_1_soma), .B(Cin), .Soma(Soma_Total), .Cout(meio_somador_2_cout));
  or or_1 (Cout, meio_somador_1_cout, meio_somador_2_cout);
endmodule

module somador_2bits (
  input  [1:0] B,
  input  [1:0] A,
  input  Cin,
  output Cout,
  output [1:0] Somas_Parciais
);

  wire somador_completo_1bit_1_cout;

  somador_completo_1bit somador_completo_1bit_1 (
    .A(A[0]), .B(B[0]), .Cin(Cin), .Soma_Total(Somas_Parciais[0]), .Cout(somador_completo_1bit_1_cout));
  somador_completo_1bit somador_completo_1bit_2 (
    .A(A[1]), .B(B[1]), .Cin(somador_completo_1bit_1_cout), .Soma_Total(Somas_Parciais[1]), .Cout(Cout));

  // Notes on the sheet:
  //   São dois somadores de 1bit
endmodule

// 4bits
module somador_4bits_4_1bit (
  input  [3:0] A,
  input  [3:0] B,
  input  Cin,
  output Cout,
  output [3:0] Somas_Parciais
);

  wire somador_completo_1bit_1_cout, somador_completo_1bit_2_cout, somador_completo_1bit_3_cout;

  somador_completo_1bit somador_completo_1bit_1 (
    .A(A[0]), .B(B[0]), .Cin(Cin), .Soma_Total(Somas_Parciais[0]), .Cout(somador_completo_1bit_1_cout));
  somador_completo_1bit somador_completo_1bit_2 (
    .A(A[1]), .B(B[1]), .Cin(somador_completo_1bit_1_cout), .Soma_Total(Somas_Parciais[1]),
    .Cout(somador_completo_1bit_2_cout));
  somador_completo_1bit somador_completo_1bit_3 (
    .A(A[2]), .B(B[2]), .Cin(somador_completo_1bit_2_cout), .Soma_Total(Somas_Parciais[2]),
    .Cout(somador_completo_1bit_3_cout));
  somador_completo_1bit somador_completo_1bit_4 (
    .A(A[3]), .B(B[3]), .Cin(somador_completo_1bit_3_cout), .Soma_Total(Somas_Parciais[3]), .Cout(Cout));
endmodule

module somador_4bits_2_2bits (
  input  [3:0] B,
  input  [3:0] A,
  input  Cin,
  output Cout,
  output [3:0] Somas_Parciais
);

  wire somador_2bits_1_cout;

  LED led_1 (.in(B[0]));
  LED led_2 (.in(B[1]));
  LED led_3 (.in(B[2]));
  LED led_4 (.in(B[3]));
  somador_2bits somador_2bits_1 (
    .Cin(Cin), .Cout(somador_2bits_1_cout), .B(B[1:0]), .A(A[1:0]), .Somas_Parciais(Somas_Parciais[1:0]));
  LED led_5 (.in(Somas_Parciais[0]));
  LED led_6 (.in(Somas_Parciais[1]));
  LED led_7 (.in(Somas_Parciais[2]));
  LED led_8 (.in(Somas_Parciais[3]));
  LED led_9 (.in(A[0]));
  LED led_10 (.in(A[1]));
  LED led_11 (.in(A[2]));
  LED led_12 (.in(A[3]));
  somador_2bits somador_2bits_2 (
    .Cin(somador_2bits_1_cout), .Cout(Cout), .B(B[3:2]), .A(A[3:2]), .Somas_Parciais(Somas_Parciais[3:2]));

  // Notes on the sheet:
  //   A contagem da ordem dos elementos começa pelo que está mais à direita
endmodule
